# Fritzing sketch sketch (saved by Fritzing 0.9.3b)
breadboards: 1

parts:
  Part1 = Arduino Nano (Rev3.0)
  M1 = fc-51 [package=THT]
  HC-SR04_Sensor_1 = HC-SR04 Ultrasonic Distance Sensor
  J1 = Piezo Speaker
  R1 = Resistor [tolerance=±5% resistance=220 package=THT]
  LED1 = smd LED [color="Red (633nm)" package="0603 [SMD]"]
  M2 = fc-51 [package=THT]
  SM2 = 28BYJ-48 Stepper Motor [part_number=28BYJ-48]
  SM3 = 28BYJ-48 Stepper Motor [part_number=28BYJ-48]
  Driver2 = 28BYJ-48 Driver Module [part_number=ULN2003 package=THT]
  Driver3 = 28BYJ-48 Driver Module [part_number=ULN2003 package=THT]
  BAT1 = BC9VPC [package=bc9vpc]
  S1 = Pushbutton [package=THT]

nets:
  N1: Part1.D2, R1.Pin_1
  N2: Part1.D3, J1.pin2
  N3: Part1.D4, HC-SR04_Sensor_1.TRIG
  N4: Part1.D5, HC-SR04_Sensor_1.ECHO
  N5: Part1.D6, M1.pin1
  N6: Part1.D7, M2.pin1
  N7: Part1.D8, Driver2.IN1
  N8: Part1.D9, Driver2.IN2
  N9: Part1.D10, Driver2.IN3
  N10: Part1.D11/MOSI, Driver2.IN4
  N11: Part1.VIN, S1.leg0
  GND: Part1.GND, M1.pin2, HC-SR04_Sensor_1.GND, J1.pin1, LED1.cathode, M2.pin2, BAT1.V-
  5V: Part1.5V, M1.pin3, HC-SR04_Sensor_1.VCC, M2.pin3
  N12: Part1.A7, Driver3.IN1
  N13: Part1.A6, Driver3.IN2
  N14: Part1.A5, Driver3.IN3
  N15: Part1.A4, Driver3.IN4
  N16: R1.Pin_0, LED1.anode
  N17: SM2.blue-pin, Driver3.blue-pin
  N18: SM2.pink-pin, Driver3.pink-pin
  N19: SM2.yellow-pin, Driver3.yellow-pin
  N20: SM2.orange-pin, Driver3.orange-pin
  N21: SM2.red-pin, Driver3.red-pin
  N22: SM3.blue-pin, Driver2.blue-pin
  N23: SM3.pink-pin, Driver2.pink-pin
  N24: SM3.yellow-pin, Driver2.yellow-pin
  N25: SM3.orange-pin, Driver2.orange-pin
  N26: SM3.red-pin, Driver2.red-pin
  N27: BAT1.V+, S1.leg1

custom parts:
  28BYJ-48 Stepper Motor: Unipolar Stepper Motor 28BYJ-48 Top coil - pink & orange Bottom coil - blue & yellow Common rail - red Connector pins: blue - pink - yellow - orange - red
  28BYJ-48 Driver Module: Generic male header
